// Logisim project TD4.circ as structural Verilog: 17 circuits, main circuit Half Adder
// HA
module Half_Adder (
  input  A,
  input  B,
  output S,
  output C
);

  xor xor_1 (S, A, B);
  and and_1 (C, A, B);
endmodule

// FA
module Full_Adder (
  input  Cin,
  input  X,
  input  Y,
  output S,
  output C0
);

  wire half_adder_1_c, half_adder_2_c, half_adder_2_s;

  Half_Adder half_adder_1 (.A(Cin), .B(half_adder_2_s), .S(S), .C(half_adder_1_c));
  Half_Adder half_adder_2 (.A(X), .B(Y), .S(half_adder_2_s), .C(half_adder_2_c));
  or or_1 (C0, half_adder_1_c, half_adder_2_c);
endmodule

// 74154
module _74154_Scale_Down (
  input  B,
  input  A,
  output Y0,
  output Y1,
  output Y2,
  output Y3
);

  wire not_1_out, not_2_out;

  not not_1 (not_1_out, B);
  not not_2 (not_2_out, A);
  nand nand_1 (Y0, not_1_out, not_2_out);
  nand nand_2 (Y1, not_1_out, A);
  nand nand_3 (Y2, B, not_2_out);
  nand nand_4 (Y3, B, A);
endmodule

// MP
module Multiplexer (
  input  C1,
  input  C0,
  input  A,
  output out_4
);

  wire and_1_out, and_2_out, not_1_out;

  not not_1 (not_1_out, A);
  and and_1 (and_1_out, C1, A);
  and and_2 (and_2_out, C0, not_1_out);
  or or_1 (out_4, and_1_out, and_2_out);
endmodule

// RN
module Register_nanka (
  input  CLOCK,
  input  RESET_minus,
  input  LOAD0_minus,
  input  LOAD1_minus,
  input  LOAD2_minus,
  input  LOAD3_minus,
  input  SELECT_A,
  input  SELECT_B,
  input  in_9,
  input  in_10,
  input  in_11,
  input  in_12
);

  wire n74153_1_p5, n74153_1_p12, n74153_2_p7, n74153_2_p14, n74153_2_p19, n74161_1_p3, n74161_1_p4,
       n74161_1_p5, n74161_1_p6, n74161_1_p7, n74161_1_p8, n74161_1_p9, n74161_2_p1, n74161_2_p8,
       n74161_2_p11, n74161_2_p13, n74161_2_p14, n74161_3_p8, n74161_3_p11, n74161_3_p12, n74161_3_p13,
       n74161_3_p14, n74161_4_p10, n74161_4_p13, n74161_4_p14, n74161_4_p15, n74161_4_p16, n74161_4_p17,
       undriven, undriven_2, undriven_3;

  // _74161 74161_1: pin names not known; wires that end beside it: RESET_minus, CLOCK, n74161_1_p3, n74161_1_p4, n74161_1_p5, n74161_1_p6, n74161_1_p7, n74161_1_p8, n74161_1_p9, n74161_1_p6
  // _74161 74161_2: pin names not known; wires that end beside it: n74161_2_p1, 1'b1, RESET_minus, CLOCK, n74161_1_p3, n74161_1_p4, n74161_1_p5, n74161_2_p8, 1'b1, LOAD0_minus, n74161_2_p11, in_12, n74161_2_p13, n74161_2_p14, n74161_2_p11
  // _74161 74161_3: pin names not known; wires that end beside it: n74161_2_p1, 1'b1, RESET_minus, CLOCK, n74161_1_p3, n74161_1_p4, n74161_1_p5, n74161_3_p8, 1'b1, LOAD1_minus, n74161_3_p11, n74161_3_p12, n74161_3_p13, n74161_3_p14, n74161_3_p11
  // _74161 74161_4: pin names not known; wires that end beside it: n74161_2_p1, 1'b1, RESET_minus, CLOCK, n74161_1_p3, n74161_1_p4, n74161_1_p5, n74161_2_p1, 1'b1, n74161_4_p10, 1'b1, LOAD2_minus, n74161_4_p13, n74161_4_p14, n74161_4_p15, n74161_4_p16, n74161_4_p17, 1'b1, LOAD3_minus, n74161_4_p13
  LED led_1 (.in(n74161_4_p10));
  LED led_2 (.in(n74161_3_p12));
  LED led_3 (.in(n74161_3_p14));
  LED led_4 (.in(n74161_3_p13));
  // _74153 74153_1: pin names not known; wires that end beside it: 1'b1, SELECT_B, 1'b1, n74161_1_p7, n74153_1_p5, 1'b1, SELECT_A, 1'b1, in_11, n74161_2_p13, n74161_1_p8, n74153_1_p12
  // _74153 74153_2: pin names not known; wires that end beside it: 1'b1, SELECT_B, 1'b1, in_10, n74161_2_p14, n74161_1_p9, n74153_2_p7, 1'b1, SELECT_A, 1'b1, in_9, n74161_3_p8, n74161_2_p8, n74153_2_p14, n74161_4_p14, n74161_4_p15, n74161_4_p16, n74161_4_p17, n74153_2_p19
  _74283 u_74283_1 (
    .C0(1'b1), .A1(n74153_1_p12), .A2(n74153_1_p5), .A3(n74153_2_p14), .A4(n74153_2_p7), .B1(n74153_2_p19),
    .B2(undriven), .B3(undriven_2), .B4(undriven_3), .\Σ1 (n74161_2_p1), .\Σ2 (n74161_1_p5),
    .\Σ3 (n74161_1_p4), .\Σ4 (n74161_1_p3));  // open: C4
  // _7474 7474_1: pin names not known
endmodule

module aaa (
  input  [3:0] in_1,
  input  A0,
  input  A1,
  input  A2,
  input  A3,
  input  [1:0] in_6,
  input  [3:0] in_7,
  input  [1:0] in_8,
  input  in_9,
  input  A0_2,
  input  A1_2,
  input  A2_2,
  input  A3_2,
  output out_14
);

  wire multiplexer_2_out;
  wire [3:0] demultiplexer_1_out0, demultiplexer_1_out1;

  DotMatrix #(.matrixcols(4), .matrixrows(1)) dotmatrix_1 (
    .col0(demultiplexer_1_out0[3]), .col1(demultiplexer_1_out0[2]), .col2(demultiplexer_1_out0[1]),
    .col3(demultiplexer_1_out0[0]));
  Demultiplexer #(.width(4)) demultiplexer_1 (
    .out0(demultiplexer_1_out0), .out1(demultiplexer_1_out1), .in({A3_2, A2_2, A1_2, A0_2}), .sel(out_14));  // open: en
  Multiplexer_part #(.select(2)) multiplexer_1 (.in0(A0), .in1(A1), .in2(A2), .in3(A3), .sel(in_6));  // open: out, en
  Hex_Digit_Display hex_digit_display_1 (.value(in_1));  // open: dp
  Multiplexer_part #(.select(2)) multiplexer_2 (
    .in0(in_7[3]), .in1(in_7[2]), .in2(in_7[1]), .in3(in_7[0]), .out(multiplexer_2_out), .sel(in_8));  // open: en
endmodule

module _74283 (
  input  C0,
  input  A1,
  input  A2,
  input  A3,
  input  A4,
  input  B1,
  input  B2,
  input  B3,
  input  B4,
  output \Σ1 ,
  output \Σ2 ,
  output \Σ3 ,
  output \Σ4 ,
  output C4
);

  wire full_adder_1_c0, full_adder_2_c0, full_adder_3_c0;

  Full_Adder full_adder_1 (.Cin(C0), .X(A1), .Y(B1), .S(\Σ1 ), .C0(full_adder_1_c0));
  Full_Adder full_adder_2 (.Cin(full_adder_1_c0), .X(A2), .Y(B2), .S(\Σ2 ), .C0(full_adder_2_c0));
  Full_Adder full_adder_3 (.Cin(full_adder_2_c0), .X(A3), .Y(B3), .S(\Σ3 ), .C0(full_adder_3_c0));
  Full_Adder full_adder_4 (.Cin(full_adder_3_c0), .X(A4), .Y(B4), .S(\Σ4 ), .C0(C4));
endmodule

module _4bit_Adder_2 (
  input  C0,
  input  [3:0] A_num,
  input  [3:0] B_num,
  output [3:0] out_4,
  output C4
);

  wire full_adder_1_c0, full_adder_2_c0, full_adder_3_c0;

  Full_Adder full_adder_1 (.Cin(C0), .X(A_num[0]), .Y(B_num[0]), .S(out_4[0]), .C0(full_adder_1_c0));
  Full_Adder full_adder_2 (.Cin(full_adder_1_c0), .X(A_num[1]), .Y(B_num[1]), .S(out_4[1]), .C0(full_adder_2_c0));
  Full_Adder full_adder_3 (.Cin(full_adder_2_c0), .X(A_num[2]), .Y(B_num[2]), .S(out_4[2]), .C0(full_adder_3_c0));
  Full_Adder full_adder_4 (.Cin(full_adder_3_c0), .X(A_num[3]), .Y(B_num[3]), .S(out_4[3]), .C0(C4));
endmodule

// DCD
module Decorder (
  input  [3:0] OPCord,
  input  C_Flag_minus,
  output [3:0] SELECT_Register,
  output [1:0] SELECT_AB
);

  wire and_1_out, not_1_out, not_2_out, not_3_out, not_4_out, not_5_out;

  not not_1 (not_1_out, OPCord[2]);
  not not_2 (not_2_out, OPCord[3]);
  not not_3 (not_3_out, OPCord[2]);
  not not_4 (not_4_out, OPCord[3]);
  not not_5 (not_5_out, OPCord[0]);
  and and_1 (and_1_out, not_5_out, C_Flag_minus);
  or or_1 (SELECT_Register[3], OPCord[3], OPCord[2]);
  or or_2 (SELECT_Register[2], not_1_out, OPCord[3]);
  or or_3 (SELECT_Register[1], not_2_out, OPCord[2]);
  or or_4 (SELECT_Register[0], not_3_out, not_4_out, and_1_out);
  or or_5 (SELECT_AB[0], OPCord[0], OPCord[3]);

  assign SELECT_AB[1] = OPCord[1];
endmodule

module Decorder_2 (
  input  [3:0] OPCord,
  input  C_Flag_minus,
  output [3:0] SELECT_Register,
  output [1:0] SELECT_AB
);

  wire and_1_out, not_1_out, not_2_out, not_3_out, not_4_out, not_5_out;

  not not_1 (not_1_out, OPCord[2]);
  not not_2 (not_2_out, OPCord[3]);
  not not_3 (not_3_out, OPCord[0]);
  or or_1 (SELECT_Register[3], OPCord[3], OPCord[2]);
  not not_4 (not_4_out, OPCord[2]);
  or or_2 (SELECT_Register[2], not_4_out, OPCord[3]);
  not not_5 (not_5_out, OPCord[3]);
  or or_3 (SELECT_Register[1], not_5_out, OPCord[2]);
  or or_4 (SELECT_Register[0], not_1_out, not_2_out, and_1_out);
  and and_1 (and_1_out, not_3_out, C_Flag_minus);
  or or_5 (SELECT_AB[0], OPCord[0], OPCord[3]);

  assign SELECT_AB[1] = OPCord[1];
endmodule

module ROMyou (
  input  in_1,
  input  in_2,
  input  in_3,
  input  in_4,
  input  in_5,
  input  in_6,
  input  in_7,
  input  in_8,
  input  in_9,
  input  in_10,
  input  in_11,
  input  in_12,
  input  in_13,
  input  in_14,
  input  in_15,
  input  in_16,
  output out_17,
  output out_18,
  output out_19,
  output out_20,
  output out_21,
  output out_22,
  output out_23,
  output out_24
);

  or or_1 (out_17, in_16, in_1);
  or or_2 (out_18, in_15, in_2);
  or or_3 (out_19, in_14, in_3);
  or or_4 (out_20, in_13, in_4);
  or or_5 (out_21, in_12, in_5);
  or or_6 (out_23, in_10, in_7);
  or or_7 (out_22, in_11, in_6);
  or or_8 (out_24, in_9, in_8);
endmodule

module ROM (
  input  [3:0] Address_in,
  output [3:0] out_2,
  output [3:0] out_3
);

  wire and_1_out, and_2_out, and_3_out, and_4_out, and_5_out, and_6_out, and_7_out, and_8_out, and_9_out,
       and_10_out, and_11_out, and_12_out, and_13_out, and_14_out, and_15_out, and_16_out, and_17_out,
       and_18_out, and_19_out, and_20_out, and_21_out, and_22_out, and_23_out, and_24_out, and_25_out,
       and_26_out, and_27_out, and_28_out, and_29_out, and_30_out, and_31_out, and_32_out, and_33_out,
       and_34_out, and_35_out, and_36_out, and_37_out, and_38_out, and_39_out, and_40_out, and_41_out,
       and_42_out, and_43_out, and_44_out, and_45_out, and_46_out, and_47_out, and_48_out, and_49_out,
       and_50_out, and_51_out, and_52_out, and_53_out, and_54_out, and_55_out, and_56_out, and_57_out,
       and_58_out, and_59_out, and_60_out, and_61_out, and_62_out, and_63_out, and_64_out, and_65_out,
       and_66_out, and_67_out, and_68_out, and_69_out, and_70_out, and_71_out, and_72_out, and_73_out,
       and_74_out, and_75_out, and_76_out, and_77_out, and_78_out, and_79_out, and_80_out, and_81_out,
       and_82_out, and_83_out, and_84_out, and_85_out, and_86_out, and_87_out, and_88_out, and_89_out,
       and_90_out, and_91_out, and_92_out, and_93_out, and_94_out, and_95_out, and_96_out, and_97_out,
       and_98_out, and_99_out, and_100_out, and_101_out, and_102_out, and_103_out, and_104_out, and_105_out,
       and_106_out, and_107_out, and_108_out, and_109_out, and_110_out, and_111_out, and_112_out,
       and_113_out, and_114_out, and_115_out, and_116_out, and_117_out, and_118_out, and_119_out,
       and_120_out, and_121_out, and_122_out, and_123_out, and_124_out, and_125_out, and_126_out,
       and_127_out, and_128_out, and_129_out, and_130_out, and_131_out, and_132_out, and_133_out,
       and_134_out, and_135_out, and_136_out, and_137_out, and_138_out, and_139_out, and_140_out,
       and_141_out, and_142_out, and_143_out, and_144_out, not_1_out, not_2_out, not_3_out, not_4_out,
       romyou_1_out_17, romyou_1_out_18, romyou_1_out_19, romyou_1_out_20, romyou_1_out_21, romyou_1_out_22,
       romyou_1_out_23, romyou_1_out_24, romyou_2_out_17, romyou_2_out_18, romyou_2_out_19, romyou_2_out_20,
       romyou_2_out_21, romyou_2_out_22, romyou_2_out_23, romyou_2_out_24, romyou_3_out_17, romyou_3_out_18,
       romyou_3_out_19, romyou_3_out_20, romyou_3_out_21, romyou_3_out_22, romyou_3_out_23, romyou_3_out_24,
       romyou_4_out_17, romyou_4_out_18, romyou_4_out_19, romyou_4_out_20, romyou_4_out_21, romyou_4_out_22,
       romyou_4_out_23, romyou_4_out_24, romyou_5_out_17, romyou_5_out_18, romyou_5_out_19, romyou_5_out_20,
       romyou_5_out_21, romyou_5_out_22, romyou_5_out_23, romyou_5_out_24, romyou_6_out_17, romyou_6_out_18,
       romyou_6_out_19, romyou_6_out_20, romyou_6_out_21, romyou_6_out_22, romyou_6_out_23, romyou_6_out_24,
       romyou_7_out_17, romyou_7_out_18, romyou_7_out_19, romyou_7_out_20, romyou_7_out_21, romyou_7_out_22,
       romyou_7_out_23, romyou_7_out_24, romyou_8_out_17, romyou_8_out_18, romyou_8_out_19, romyou_8_out_20,
       romyou_8_out_21, romyou_8_out_22, romyou_8_out_23, romyou_8_out_24, romyou_9_out_17, romyou_9_out_18,
       romyou_9_out_19, romyou_9_out_20, romyou_9_out_21, romyou_9_out_22, romyou_9_out_23, romyou_9_out_24,
       romyou_10_out_17, romyou_10_out_18, romyou_10_out_19, romyou_10_out_20, romyou_10_out_21,
       romyou_10_out_22, romyou_10_out_23, romyou_10_out_24, romyou_11_out_17, romyou_11_out_18,
       romyou_11_out_19, romyou_11_out_20, romyou_11_out_21, romyou_11_out_22, romyou_11_out_23,
       romyou_11_out_24, romyou_12_out_17, romyou_12_out_18, romyou_12_out_19, romyou_12_out_20,
       romyou_12_out_21, romyou_12_out_22, romyou_12_out_23, romyou_12_out_24, romyou_13_out_17,
       romyou_13_out_18, romyou_13_out_19, romyou_13_out_20, romyou_13_out_21, romyou_13_out_22,
       romyou_13_out_23, romyou_13_out_24, romyou_14_out_17, romyou_14_out_18, romyou_14_out_19,
       romyou_14_out_20, romyou_14_out_21, romyou_14_out_22, romyou_14_out_23, romyou_14_out_24,
       romyou_15_out_17, romyou_15_out_18, romyou_15_out_19, romyou_15_out_20, romyou_15_out_21,
       romyou_15_out_22, romyou_15_out_23, romyou_15_out_24;

  not not_1 (not_1_out, Address_in[0]);
  not not_2 (not_2_out, Address_in[1]);
  not not_3 (not_3_out, Address_in[2]);
  not not_4 (not_4_out, Address_in[3]);
  and and_1 (and_1_out, not_1_out, not_2_out, not_3_out, not_4_out);
  and and_2 (and_2_out, and_1_out, 1'b1);
  and and_3 (and_3_out, and_1_out, 1'b0);
  and and_4 (and_4_out, not_2_out, not_3_out, not_4_out, Address_in[0]);
  and and_5 (and_5_out, and_4_out, 1'b0);
  and and_6 (and_6_out, and_4_out, 1'b0);
  and and_7 (and_7_out, not_1_out, not_3_out, not_4_out, Address_in[1]);
  and and_8 (and_8_out, and_7_out, 1'b1);
  and and_9 (and_9_out, and_7_out, 1'b1);
  and and_10 (and_10_out, not_3_out, not_4_out, Address_in[0], Address_in[1]);
  and and_11 (and_11_out, and_10_out, 1'b0);
  and and_12 (and_12_out, and_10_out, 1'b0);
  and and_13 (and_13_out, not_1_out, not_2_out, Address_in[2], not_4_out);
  and and_14 (and_14_out, and_13_out, 1'b1);
  and and_15 (and_15_out, and_13_out, 1'b1);
  and and_16 (and_16_out, Address_in[0], not_2_out, Address_in[2], not_4_out);
  and and_17 (and_17_out, and_16_out, 1'b0);
  and and_18 (and_18_out, and_16_out, 1'b1);
  and and_19 (and_19_out, not_1_out, Address_in[1], Address_in[2], not_4_out);
  and and_20 (and_20_out, and_19_out, 1'b0);
  and and_21 (and_21_out, and_19_out, 1'b0);
  and and_22 (and_22_out, Address_in[0], Address_in[1], Address_in[2], not_4_out);
  and and_23 (and_23_out, and_22_out, 1'b1);
  and and_24 (and_24_out, and_22_out, 1'b1);
  and and_25 (and_25_out, not_1_out, not_2_out, not_3_out, Address_in[3]);
  and and_26 (and_26_out, and_25_out, 1'b0);
  and and_27 (and_27_out, and_25_out, 1'b0);
  and and_28 (and_28_out, Address_in[0], not_2_out, not_3_out, Address_in[3]);
  and and_29 (and_29_out, and_28_out, 1'b1);
  and and_30 (and_30_out, and_28_out, 1'b1);
  and and_31 (and_31_out, not_1_out, Address_in[1], not_3_out, Address_in[3]);
  and and_32 (and_32_out, and_31_out, 1'b1);
  and and_33 (and_33_out, and_31_out, 1'b0);
  and and_34 (and_34_out, Address_in[0], Address_in[1], not_3_out, Address_in[3]);
  and and_35 (and_35_out, and_34_out, 1'b0);
  and and_36 (and_36_out, and_34_out, 1'b1);
  and and_37 (and_37_out, not_1_out, not_2_out, Address_in[2], Address_in[3]);
  and and_38 (and_38_out, and_37_out, 1'b0);
  and and_39 (and_39_out, and_37_out, 1'b0);
  and and_40 (and_40_out, Address_in[0], not_2_out, Address_in[2], Address_in[3]);
  and and_41 (and_41_out, and_40_out, 1'b1);
  and and_42 (and_42_out, and_40_out, 1'b1);
  and and_43 (and_43_out, not_1_out, Address_in[1], Address_in[2], Address_in[3]);
  and and_44 (and_44_out, and_43_out, 1'b0);
  and and_45 (and_45_out, and_43_out, 1'b1);
  and and_46 (and_46_out, Address_in[0], Address_in[1], Address_in[2], Address_in[3]);
  and and_47 (and_47_out, and_46_out, 1'b1);
  and and_48 (and_48_out, and_46_out, 1'b1);
  and and_49 (and_49_out, and_1_out, 1'b1);
  and and_50 (and_50_out, and_1_out, 1'b1);
  and and_51 (and_51_out, and_4_out, 1'b0);
  and and_52 (and_52_out, and_4_out, 1'b0);
  and and_53 (and_53_out, and_7_out, 1'b1);
  and and_54 (and_54_out, and_7_out, 1'b0);
  and and_55 (and_55_out, and_10_out, 1'b0);
  and and_56 (and_56_out, and_10_out, 1'b0);
  and and_57 (and_57_out, and_13_out, 1'b1);
  and and_58 (and_58_out, and_13_out, 1'b0);
  and and_59 (and_59_out, and_16_out, 1'b1);
  and and_60 (and_60_out, and_16_out, 1'b1);
  and and_61 (and_61_out, and_19_out, 1'b0);
  and and_62 (and_62_out, and_19_out, 1'b0);
  and and_63 (and_63_out, and_22_out, 1'b0);
  and and_64 (and_64_out, and_22_out, 1'b1);
  and and_65 (and_65_out, and_25_out, 1'b0);
  and and_66 (and_66_out, and_25_out, 1'b0);
  and and_67 (and_67_out, and_28_out, 1'b0);
  and and_68 (and_68_out, and_28_out, 1'b1);
  and and_69 (and_69_out, and_31_out, 1'b1);
  and and_70 (and_70_out, and_31_out, 1'b1);
  and and_71 (and_71_out, and_34_out, 1'b1);
  and and_72 (and_72_out, and_34_out, 1'b1);
  and and_73 (and_73_out, and_37_out, 1'b0);
  and and_74 (and_74_out, and_37_out, 1'b0);
  and and_75 (and_75_out, and_40_out, 1'b0);
  and and_76 (and_76_out, and_40_out, 1'b1);
  and and_77 (and_77_out, and_43_out, 1'b1);
  and and_78 (and_78_out, and_43_out, 1'b1);
  and and_79 (and_79_out, and_46_out, 1'b1);
  and and_80 (and_80_out, and_46_out, 1'b1);
  and and_81 (and_81_out, and_1_out, 1'b1);
  and and_82 (and_82_out, and_1_out, 1'b0);
  and and_83 (and_83_out, and_4_out, 1'b0);
  and and_84 (and_84_out, and_4_out, 1'b0);
  and and_85 (and_85_out, and_7_out, 1'b0);
  and and_86 (and_86_out, and_7_out, 1'b0);
  and and_87 (and_87_out, and_10_out, 1'b0);
  and and_88 (and_88_out, and_10_out, 1'b0);
  and and_89 (and_89_out, and_13_out, 1'b0);
  and and_90 (and_90_out, and_13_out, 1'b0);
  and and_91 (and_91_out, and_16_out, 1'b0);
  and and_92 (and_92_out, and_16_out, 1'b1);
  and and_93 (and_93_out, and_19_out, 1'b0);
  and and_94 (and_94_out, and_19_out, 1'b0);
  and and_95 (and_95_out, and_22_out, 1'b1);
  and and_96 (and_96_out, and_22_out, 1'b0);
  and and_97 (and_97_out, and_25_out, 1'b0);
  and and_98 (and_98_out, and_25_out, 1'b0);
  and and_99 (and_99_out, and_28_out, 1'b0);
  and and_100 (and_100_out, and_28_out, 1'b1);
  and and_101 (and_101_out, and_31_out, 1'b0);
  and and_102 (and_102_out, and_31_out, 1'b0);
  and and_103 (and_103_out, and_34_out, 1'b1);
  and and_104 (and_104_out, and_34_out, 1'b0);
  and and_105 (and_105_out, and_37_out, 1'b0);
  and and_106 (and_106_out, and_37_out, 1'b0);
  and and_107 (and_107_out, and_40_out, 1'b0);
  and and_108 (and_108_out, and_40_out, 1'b1);
  and and_109 (and_109_out, and_43_out, 1'b1);
  and and_110 (and_110_out, and_43_out, 1'b0);
  and and_111 (and_111_out, and_46_out, 1'b1);
  and and_112 (and_112_out, and_46_out, 1'b1);
  and and_113 (and_113_out, and_1_out, 1'b1);
  and and_114 (and_114_out, and_1_out, 1'b1);
  and and_115 (and_115_out, and_4_out, 1'b0);
  and and_116 (and_116_out, and_4_out, 1'b1);
  and and_117 (and_117_out, and_7_out, 1'b1);
  and and_118 (and_118_out, and_7_out, 1'b0);
  and and_119 (and_119_out, and_10_out, 1'b1);
  and and_120 (and_120_out, and_10_out, 1'b0);
  and and_121 (and_121_out, and_13_out, 1'b1);
  and and_122 (and_122_out, and_13_out, 1'b1);
  and and_123 (and_123_out, and_16_out, 1'b1);
  and and_124 (and_124_out, and_16_out, 1'b0);
  and and_125 (and_125_out, and_19_out, 1'b1);
  and and_126 (and_126_out, and_19_out, 1'b0);
  and and_127 (and_127_out, and_22_out, 1'b0);
  and and_128 (and_128_out, and_22_out, 1'b1);
  and and_129 (and_129_out, and_25_out, 1'b0);
  and and_130 (and_130_out, and_25_out, 1'b1);
  and and_131 (and_131_out, and_28_out, 1'b0);
  and and_132 (and_132_out, and_28_out, 1'b0);
  and and_133 (and_133_out, and_31_out, 1'b0);
  and and_134 (and_134_out, and_31_out, 1'b0);
  and and_135 (and_135_out, and_34_out, 1'b0);
  and and_136 (and_136_out, and_34_out, 1'b0);
  and and_137 (and_137_out, and_37_out, 1'b0);
  and and_138 (and_138_out, and_37_out, 1'b1);
  and and_139 (and_139_out, and_40_out, 1'b1);
  and and_140 (and_140_out, and_40_out, 1'b0);
  and and_141 (and_141_out, and_43_out, 1'b0);
  and and_142 (and_142_out, and_43_out, 1'b0);
  and and_143 (and_143_out, and_46_out, 1'b1);
  and and_144 (and_144_out, and_46_out, 1'b1);
  ROMyou romyou_1 (
    .in_9(and_113_out), .in_10(and_114_out), .in_11(and_81_out), .in_12(and_82_out), .in_13(and_49_out),
    .in_14(and_50_out), .in_15(and_3_out), .in_16(and_2_out), .in_1(1'b0), .in_2(1'b0), .in_3(1'b0),
    .in_4(1'b0), .in_5(1'b0), .in_6(1'b0), .in_7(1'b0), .in_8(1'b0), .out_17(romyou_1_out_17),
    .out_18(romyou_1_out_18), .out_19(romyou_1_out_19), .out_20(romyou_1_out_20), .out_21(romyou_1_out_21),
    .out_22(romyou_1_out_22), .out_23(romyou_1_out_23), .out_24(romyou_1_out_24));
  ROMyou romyou_2 (
    .in_9(and_116_out), .in_10(and_115_out), .in_11(and_83_out), .in_12(and_84_out), .in_13(and_51_out),
    .in_14(and_52_out), .in_15(and_6_out), .in_16(and_5_out), .in_1(romyou_1_out_17), .in_2(romyou_1_out_18),
    .in_3(romyou_1_out_19), .in_4(romyou_1_out_20), .in_5(romyou_1_out_21), .in_6(romyou_1_out_22),
    .in_7(romyou_1_out_23), .in_8(romyou_1_out_24), .out_17(romyou_2_out_17), .out_18(romyou_2_out_18),
    .out_19(romyou_2_out_19), .out_20(romyou_2_out_20), .out_21(romyou_2_out_21), .out_22(romyou_2_out_22),
    .out_23(romyou_2_out_23), .out_24(romyou_2_out_24));
  ROMyou romyou_3 (
    .in_9(and_117_out), .in_10(and_118_out), .in_11(and_85_out), .in_12(and_86_out), .in_13(and_54_out),
    .in_14(and_53_out), .in_15(and_8_out), .in_16(and_9_out), .in_1(romyou_2_out_17), .in_2(romyou_2_out_18),
    .in_3(romyou_2_out_19), .in_4(romyou_2_out_20), .in_5(romyou_2_out_21), .in_6(romyou_2_out_22),
    .in_7(romyou_2_out_23), .in_8(romyou_2_out_24), .out_17(romyou_3_out_17), .out_18(romyou_3_out_18),
    .out_19(romyou_3_out_19), .out_20(romyou_3_out_20), .out_21(romyou_3_out_21), .out_22(romyou_3_out_22),
    .out_23(romyou_3_out_23), .out_24(romyou_3_out_24));
  ROMyou romyou_4 (
    .in_9(and_119_out), .in_10(and_120_out), .in_11(and_87_out), .in_12(and_88_out), .in_13(and_56_out),
    .in_14(and_55_out), .in_15(and_11_out), .in_16(and_12_out), .in_1(romyou_3_out_17),
    .in_2(romyou_3_out_18), .in_3(romyou_3_out_19), .in_4(romyou_3_out_20), .in_5(romyou_3_out_21),
    .in_6(romyou_3_out_22), .in_7(romyou_3_out_23), .in_8(romyou_3_out_24), .out_17(romyou_4_out_17),
    .out_18(romyou_4_out_18), .out_19(romyou_4_out_19), .out_20(romyou_4_out_20), .out_21(romyou_4_out_21),
    .out_22(romyou_4_out_22), .out_23(romyou_4_out_23), .out_24(romyou_4_out_24));
  ROMyou romyou_5 (
    .in_9(and_121_out), .in_10(and_122_out), .in_11(and_89_out), .in_12(and_90_out), .in_13(and_58_out),
    .in_14(and_57_out), .in_15(and_14_out), .in_16(and_15_out), .in_1(romyou_4_out_17),
    .in_2(romyou_4_out_18), .in_3(romyou_4_out_19), .in_4(romyou_4_out_20), .in_5(romyou_4_out_21),
    .in_6(romyou_4_out_22), .in_7(romyou_4_out_23), .in_8(romyou_4_out_24), .out_17(romyou_5_out_17),
    .out_18(romyou_5_out_18), .out_19(romyou_5_out_19), .out_20(romyou_5_out_20), .out_21(romyou_5_out_21),
    .out_22(romyou_5_out_22), .out_23(romyou_5_out_23), .out_24(romyou_5_out_24));
  ROMyou romyou_6 (
    .in_9(and_124_out), .in_10(and_123_out), .in_11(and_92_out), .in_12(and_91_out), .in_13(and_60_out),
    .in_14(and_59_out), .in_15(and_17_out), .in_16(and_18_out), .in_1(romyou_5_out_17),
    .in_2(romyou_5_out_18), .in_3(romyou_5_out_19), .in_4(romyou_5_out_20), .in_5(romyou_5_out_21),
    .in_6(romyou_5_out_22), .in_7(romyou_5_out_23), .in_8(romyou_5_out_24), .out_17(romyou_6_out_17),
    .out_18(romyou_6_out_18), .out_19(romyou_6_out_19), .out_20(romyou_6_out_20), .out_21(romyou_6_out_21),
    .out_22(romyou_6_out_22), .out_23(romyou_6_out_23), .out_24(romyou_6_out_24));
  ROMyou romyou_7 (
    .in_9(and_125_out), .in_10(and_126_out), .in_11(and_94_out), .in_12(and_93_out), .in_13(and_61_out),
    .in_14(and_62_out), .in_15(and_21_out), .in_16(and_20_out), .in_1(romyou_6_out_17),
    .in_2(romyou_6_out_18), .in_3(romyou_6_out_19), .in_4(romyou_6_out_20), .in_5(romyou_6_out_21),
    .in_6(romyou_6_out_22), .in_7(romyou_6_out_23), .in_8(romyou_6_out_24), .out_17(romyou_7_out_17),
    .out_18(romyou_7_out_18), .out_19(romyou_7_out_19), .out_20(romyou_7_out_20), .out_21(romyou_7_out_21),
    .out_22(romyou_7_out_22), .out_23(romyou_7_out_23), .out_24(romyou_7_out_24));
  ROMyou romyou_8 (
    .in_9(and_127_out), .in_10(and_128_out), .in_11(and_95_out), .in_12(and_96_out), .in_13(and_63_out),
    .in_14(and_64_out), .in_15(and_23_out), .in_16(and_24_out), .in_1(romyou_7_out_17),
    .in_2(romyou_7_out_18), .in_3(romyou_7_out_19), .in_4(romyou_7_out_20), .in_5(romyou_7_out_21),
    .in_6(romyou_7_out_22), .in_7(romyou_7_out_23), .in_8(romyou_7_out_24), .out_17(romyou_8_out_17),
    .out_18(romyou_8_out_18), .out_19(romyou_8_out_19), .out_20(romyou_8_out_20), .out_21(romyou_8_out_21),
    .out_22(romyou_8_out_22), .out_23(romyou_8_out_23), .out_24(romyou_8_out_24));
  ROMyou romyou_9 (
    .in_9(and_130_out), .in_10(and_129_out), .in_11(and_98_out), .in_12(and_97_out), .in_13(and_66_out),
    .in_14(and_65_out), .in_15(and_27_out), .in_16(and_26_out), .in_1(romyou_8_out_17),
    .in_2(romyou_8_out_18), .in_3(romyou_8_out_19), .in_4(romyou_8_out_20), .in_5(romyou_8_out_21),
    .in_6(romyou_8_out_22), .in_7(romyou_8_out_23), .in_8(romyou_8_out_24), .out_17(romyou_9_out_17),
    .out_18(romyou_9_out_18), .out_19(romyou_9_out_19), .out_20(romyou_9_out_20), .out_21(romyou_9_out_21),
    .out_22(romyou_9_out_22), .out_23(romyou_9_out_23), .out_24(romyou_9_out_24));
  ROMyou romyou_10 (
    .in_9(and_131_out), .in_10(and_132_out), .in_11(and_99_out), .in_12(and_100_out), .in_13(and_67_out),
    .in_14(and_68_out), .in_15(and_29_out), .in_16(and_30_out), .in_1(romyou_9_out_17),
    .in_2(romyou_9_out_18), .in_3(romyou_9_out_19), .in_4(romyou_9_out_20), .in_5(romyou_9_out_21),
    .in_6(romyou_9_out_22), .in_7(romyou_9_out_23), .in_8(romyou_9_out_24), .out_17(romyou_10_out_17),
    .out_18(romyou_10_out_18), .out_19(romyou_10_out_19), .out_20(romyou_10_out_20),
    .out_21(romyou_10_out_21), .out_22(romyou_10_out_22), .out_23(romyou_10_out_23), .out_24(romyou_10_out_24));
  ROMyou romyou_11 (
    .in_9(and_134_out), .in_10(and_133_out), .in_11(and_102_out), .in_12(and_101_out), .in_13(and_69_out),
    .in_14(and_70_out), .in_15(and_33_out), .in_16(and_32_out), .in_1(romyou_10_out_17),
    .in_2(romyou_10_out_18), .in_3(romyou_10_out_19), .in_4(romyou_10_out_20), .in_5(romyou_10_out_21),
    .in_6(romyou_10_out_22), .in_7(romyou_10_out_23), .in_8(romyou_10_out_24), .out_17(romyou_11_out_17),
    .out_18(romyou_11_out_18), .out_19(romyou_11_out_19), .out_20(romyou_11_out_20),
    .out_21(romyou_11_out_21), .out_22(romyou_11_out_22), .out_23(romyou_11_out_23), .out_24(romyou_11_out_24));
  ROMyou romyou_12 (
    .in_9(and_136_out), .in_10(and_135_out), .in_11(and_103_out), .in_12(and_104_out), .in_13(and_72_out),
    .in_14(and_71_out), .in_15(and_35_out), .in_16(and_36_out), .in_1(romyou_11_out_17),
    .in_2(romyou_11_out_18), .in_3(romyou_11_out_19), .in_4(romyou_11_out_20), .in_5(romyou_11_out_21),
    .in_6(romyou_11_out_22), .in_7(romyou_11_out_23), .in_8(romyou_11_out_24), .out_17(romyou_12_out_17),
    .out_18(romyou_12_out_18), .out_19(romyou_12_out_19), .out_20(romyou_12_out_20),
    .out_21(romyou_12_out_21), .out_22(romyou_12_out_22), .out_23(romyou_12_out_23), .out_24(romyou_12_out_24));
  ROMyou romyou_13 (
    .in_9(and_138_out), .in_10(and_137_out), .in_11(and_105_out), .in_12(and_106_out), .in_13(and_74_out),
    .in_14(and_73_out), .in_15(and_38_out), .in_16(and_39_out), .in_1(romyou_12_out_17),
    .in_2(romyou_12_out_18), .in_3(romyou_12_out_19), .in_4(romyou_12_out_20), .in_5(romyou_12_out_21),
    .in_6(romyou_12_out_22), .in_7(romyou_12_out_23), .in_8(romyou_12_out_24), .out_17(romyou_13_out_17),
    .out_18(romyou_13_out_18), .out_19(romyou_13_out_19), .out_20(romyou_13_out_20),
    .out_21(romyou_13_out_21), .out_22(romyou_13_out_22), .out_23(romyou_13_out_23), .out_24(romyou_13_out_24));
  ROMyou romyou_14 (
    .in_9(and_140_out), .in_10(and_139_out), .in_11(and_107_out), .in_12(and_108_out), .in_13(and_75_out),
    .in_14(and_76_out), .in_15(and_42_out), .in_16(and_41_out), .in_1(romyou_13_out_17),
    .in_2(romyou_13_out_18), .in_3(romyou_13_out_19), .in_4(romyou_13_out_20), .in_5(romyou_13_out_21),
    .in_6(romyou_13_out_22), .in_7(romyou_13_out_23), .in_8(romyou_13_out_24), .out_17(romyou_14_out_17),
    .out_18(romyou_14_out_18), .out_19(romyou_14_out_19), .out_20(romyou_14_out_20),
    .out_21(romyou_14_out_21), .out_22(romyou_14_out_22), .out_23(romyou_14_out_23), .out_24(romyou_14_out_24));
  ROMyou romyou_15 (
    .in_9(and_141_out), .in_10(and_142_out), .in_11(and_110_out), .in_12(and_109_out), .in_13(and_78_out),
    .in_14(and_77_out), .in_15(and_44_out), .in_16(and_45_out), .in_1(romyou_14_out_17),
    .in_2(romyou_14_out_18), .in_3(romyou_14_out_19), .in_4(romyou_14_out_20), .in_5(romyou_14_out_21),
    .in_6(romyou_14_out_22), .in_7(romyou_14_out_23), .in_8(romyou_14_out_24), .out_17(romyou_15_out_17),
    .out_18(romyou_15_out_18), .out_19(romyou_15_out_19), .out_20(romyou_15_out_20),
    .out_21(romyou_15_out_21), .out_22(romyou_15_out_22), .out_23(romyou_15_out_23), .out_24(romyou_15_out_24));
  ROMyou romyou_16 (
    .in_9(and_144_out), .in_10(and_143_out), .in_11(and_111_out), .in_12(and_112_out), .in_13(and_80_out),
    .in_14(and_79_out), .in_15(and_47_out), .in_16(and_48_out), .in_1(romyou_15_out_17),
    .in_2(romyou_15_out_18), .in_3(romyou_15_out_19), .in_4(romyou_15_out_20), .in_5(romyou_15_out_21),
    .in_6(romyou_15_out_22), .in_7(romyou_15_out_23), .in_8(romyou_15_out_24), .out_17(out_2[3]),
    .out_18(out_2[2]), .out_19(out_2[1]), .out_20(out_2[0]), .out_21(out_3[3]), .out_22(out_3[2]),
    .out_23(out_3[1]), .out_24(out_3[0]));
endmodule

module ROM_2 (
  input  [3:0] Address_in,
  output [3:0] out_2,
  output [3:0] out_3
);

  wire and_1_out, and_2_out, and_3_out, and_4_out, and_5_out, and_6_out, and_7_out, and_8_out, and_9_out,
       and_10_out, and_11_out, and_12_out, and_13_out, and_14_out, and_15_out, and_16_out, and_17_out,
       and_18_out, and_19_out, and_20_out, and_21_out, and_22_out, and_23_out, and_24_out, and_25_out,
       and_26_out, and_27_out, and_28_out, and_29_out, and_30_out, and_31_out, and_32_out, and_33_out,
       and_34_out, and_35_out, and_36_out, and_37_out, and_38_out, and_39_out, and_40_out, and_41_out,
       and_42_out, and_43_out, and_44_out, and_45_out, and_46_out, and_47_out, and_48_out, and_49_out,
       and_50_out, and_51_out, and_52_out, and_53_out, and_54_out, and_55_out, and_56_out, and_57_out,
       and_58_out, and_59_out, and_60_out, and_61_out, and_62_out, and_63_out, and_64_out, and_65_out,
       and_66_out, and_67_out, and_68_out, and_69_out, and_70_out, and_71_out, and_72_out, and_73_out,
       and_74_out, and_75_out, and_76_out, and_77_out, and_78_out, and_79_out, and_80_out, and_81_out,
       and_82_out, and_83_out, and_84_out, and_85_out, and_86_out, and_87_out, and_88_out, and_89_out,
       and_90_out, and_91_out, and_92_out, and_93_out, and_94_out, and_95_out, and_96_out, and_97_out,
       and_98_out, and_99_out, and_100_out, and_101_out, and_102_out, and_103_out, and_104_out, and_105_out,
       and_106_out, and_107_out, and_108_out, and_109_out, and_110_out, and_111_out, and_112_out,
       and_113_out, and_114_out, and_115_out, and_116_out, and_117_out, and_118_out, and_119_out,
       and_120_out, and_121_out, and_122_out, and_123_out, and_124_out, and_125_out, and_126_out,
       and_127_out, and_128_out, and_129_out, and_130_out, and_131_out, and_132_out, and_133_out,
       and_134_out, and_135_out, and_136_out, and_137_out, and_138_out, and_139_out, and_140_out,
       and_141_out, and_142_out, and_143_out, and_144_out, not_1_out, not_2_out, not_3_out, not_4_out,
       romyou_1_out_17, romyou_1_out_18, romyou_1_out_19, romyou_1_out_20, romyou_1_out_21, romyou_1_out_22,
       romyou_1_out_23, romyou_1_out_24, romyou_2_out_17, romyou_2_out_18, romyou_2_out_19, romyou_2_out_20,
       romyou_2_out_21, romyou_2_out_22, romyou_2_out_23, romyou_2_out_24, romyou_3_out_17, romyou_3_out_18,
       romyou_3_out_19, romyou_3_out_20, romyou_3_out_21, romyou_3_out_22, romyou_3_out_23, romyou_3_out_24,
       romyou_4_out_17, romyou_4_out_18, romyou_4_out_19, romyou_4_out_20, romyou_4_out_21, romyou_4_out_22,
       romyou_4_out_23, romyou_4_out_24, romyou_5_out_17, romyou_5_out_18, romyou_5_out_19, romyou_5_out_20,
       romyou_5_out_21, romyou_5_out_22, romyou_5_out_23, romyou_5_out_24, romyou_6_out_17, romyou_6_out_18,
       romyou_6_out_19, romyou_6_out_20, romyou_6_out_21, romyou_6_out_22, romyou_6_out_23, romyou_6_out_24,
       romyou_7_out_17, romyou_7_out_18, romyou_7_out_19, romyou_7_out_20, romyou_7_out_21, romyou_7_out_22,
       romyou_7_out_23, romyou_7_out_24, romyou_8_out_17, romyou_8_out_18, romyou_8_out_19, romyou_8_out_20,
       romyou_8_out_21, romyou_8_out_22, romyou_8_out_23, romyou_8_out_24, romyou_9_out_17, romyou_9_out_18,
       romyou_9_out_19, romyou_9_out_20, romyou_9_out_21, romyou_9_out_22, romyou_9_out_23, romyou_9_out_24,
       romyou_10_out_17, romyou_10_out_18, romyou_10_out_19, romyou_10_out_20, romyou_10_out_21,
       romyou_10_out_22, romyou_10_out_23, romyou_10_out_24, romyou_11_out_17, romyou_11_out_18,
       romyou_11_out_19, romyou_11_out_20, romyou_11_out_21, romyou_11_out_22, romyou_11_out_23,
       romyou_11_out_24, romyou_12_out_17, romyou_12_out_18, romyou_12_out_19, romyou_12_out_20,
       romyou_12_out_21, romyou_12_out_22, romyou_12_out_23, romyou_12_out_24, romyou_13_out_17,
       romyou_13_out_18, romyou_13_out_19, romyou_13_out_20, romyou_13_out_21, romyou_13_out_22,
       romyou_13_out_23, romyou_13_out_24, romyou_14_out_17, romyou_14_out_18, romyou_14_out_19,
       romyou_14_out_20, romyou_14_out_21, romyou_14_out_22, romyou_14_out_23, romyou_14_out_24,
       romyou_15_out_17, romyou_15_out_18, romyou_15_out_19, romyou_15_out_20, romyou_15_out_21,
       romyou_15_out_22, romyou_15_out_23, romyou_15_out_24;

  not not_1 (not_1_out, Address_in[0]);
  not not_2 (not_2_out, Address_in[1]);
  not not_3 (not_3_out, Address_in[2]);
  not not_4 (not_4_out, Address_in[3]);
  and and_1 (and_1_out, not_1_out, not_2_out, not_3_out, not_4_out);
  and and_2 (and_2_out, and_1_out, 1'b1);
  and and_3 (and_3_out, and_1_out, 1'b0);
  and and_4 (and_4_out, not_2_out, not_3_out, not_4_out, Address_in[0]);
  and and_5 (and_5_out, and_4_out, 1'b0);
  and and_6 (and_6_out, and_4_out, 1'b0);
  and and_7 (and_7_out, not_1_out, not_3_out, not_4_out, Address_in[1]);
  and and_8 (and_8_out, and_7_out, 1'b1);
  and and_9 (and_9_out, and_7_out, 1'b1);
  and and_10 (and_10_out, not_3_out, not_4_out, Address_in[0], Address_in[1]);
  and and_11 (and_11_out, and_10_out, 1'b0);
  and and_12 (and_12_out, and_10_out, 1'b0);
  and and_13 (and_13_out, not_1_out, not_2_out, Address_in[2], not_4_out);
  and and_14 (and_14_out, and_13_out, 1'b1);
  and and_15 (and_15_out, and_13_out, 1'b1);
  and and_16 (and_16_out, Address_in[0], not_2_out, Address_in[2], not_4_out);
  and and_17 (and_17_out, and_16_out, 1'b1);
  and and_18 (and_18_out, and_16_out, 1'b0);
  and and_19 (and_19_out, not_1_out, Address_in[1], Address_in[2], not_4_out);
  and and_20 (and_20_out, and_19_out, 1'b0);
  and and_21 (and_21_out, and_19_out, 1'b0);
  and and_22 (and_22_out, Address_in[0], Address_in[1], Address_in[2], not_4_out);
  and and_23 (and_23_out, and_22_out, 1'b1);
  and and_24 (and_24_out, and_22_out, 1'b1);
  and and_25 (and_25_out, not_1_out, not_2_out, not_3_out, Address_in[3]);
  and and_26 (and_26_out, and_25_out, 1'b0);
  and and_27 (and_27_out, and_25_out, 1'b0);
  and and_28 (and_28_out, Address_in[0], not_2_out, not_3_out, Address_in[3]);
  and and_29 (and_29_out, and_28_out, 1'b1);
  and and_30 (and_30_out, and_28_out, 1'b1);
  and and_31 (and_31_out, not_1_out, Address_in[1], not_3_out, Address_in[3]);
  and and_32 (and_32_out, and_31_out, 1'b0);
  and and_33 (and_33_out, and_31_out, 1'b1);
  and and_34 (and_34_out, Address_in[0], Address_in[1], not_3_out, Address_in[3]);
  and and_35 (and_35_out, and_34_out, 1'b1);
  and and_36 (and_36_out, and_34_out, 1'b0);
  and and_37 (and_37_out, not_1_out, not_2_out, Address_in[2], Address_in[3]);
  and and_38 (and_38_out, and_37_out, 1'b0);
  and and_39 (and_39_out, and_37_out, 1'b0);
  and and_40 (and_40_out, Address_in[0], not_2_out, Address_in[2], Address_in[3]);
  and and_41 (and_41_out, and_40_out, 1'b1);
  and and_42 (and_42_out, and_40_out, 1'b1);
  and and_43 (and_43_out, not_1_out, Address_in[1], Address_in[2], Address_in[3]);
  and and_44 (and_44_out, and_43_out, 1'b1);
  and and_45 (and_45_out, and_43_out, 1'b0);
  and and_46 (and_46_out, Address_in[0], Address_in[1], Address_in[2], Address_in[3]);
  and and_47 (and_47_out, and_46_out, 1'b1);
  and and_48 (and_48_out, and_46_out, 1'b1);
  and and_49 (and_49_out, and_1_out, 1'b1);
  and and_50 (and_50_out, and_1_out, 1'b1);
  and and_51 (and_51_out, and_4_out, 1'b0);
  and and_52 (and_52_out, and_4_out, 1'b0);
  and and_53 (and_53_out, and_7_out, 1'b0);
  and and_54 (and_54_out, and_7_out, 1'b1);
  and and_55 (and_55_out, and_10_out, 1'b0);
  and and_56 (and_56_out, and_10_out, 1'b0);
  and and_57 (and_57_out, and_13_out, 1'b1);
  and and_58 (and_58_out, and_13_out, 1'b0);
  and and_59 (and_59_out, and_16_out, 1'b1);
  and and_60 (and_60_out, and_16_out, 1'b1);
  and and_61 (and_61_out, and_19_out, 1'b0);
  and and_62 (and_62_out, and_19_out, 1'b0);
  and and_63 (and_63_out, and_22_out, 1'b0);
  and and_64 (and_64_out, and_22_out, 1'b1);
  and and_65 (and_65_out, and_25_out, 1'b0);
  and and_66 (and_66_out, and_25_out, 1'b0);
  and and_67 (and_67_out, and_28_out, 1'b0);
  and and_68 (and_68_out, and_28_out, 1'b1);
  and and_69 (and_69_out, and_31_out, 1'b1);
  and and_70 (and_70_out, and_31_out, 1'b1);
  and and_71 (and_71_out, and_34_out, 1'b1);
  and and_72 (and_72_out, and_34_out, 1'b1);
  and and_73 (and_73_out, and_37_out, 1'b0);
  and and_74 (and_74_out, and_37_out, 1'b0);
  and and_75 (and_75_out, and_40_out, 1'b1);
  and and_76 (and_76_out, and_40_out, 1'b0);
  and and_77 (and_77_out, and_43_out, 1'b1);
  and and_78 (and_78_out, and_43_out, 1'b1);
  and and_79 (and_79_out, and_46_out, 1'b1);
  and and_80 (and_80_out, and_46_out, 1'b1);
  and and_81 (and_81_out, and_1_out, 1'b1);
  and and_82 (and_82_out, and_1_out, 1'b0);
  and and_83 (and_83_out, and_4_out, 1'b0);
  and and_84 (and_84_out, and_4_out, 1'b0);
  and and_85 (and_85_out, and_7_out, 1'b0);
  and and_86 (and_86_out, and_7_out, 1'b0);
  and and_87 (and_87_out, and_10_out, 1'b0);
  and and_88 (and_88_out, and_10_out, 1'b0);
  and and_89 (and_89_out, and_13_out, 1'b0);
  and and_90 (and_90_out, and_13_out, 1'b0);
  and and_91 (and_91_out, and_16_out, 1'b1);
  and and_92 (and_92_out, and_16_out, 1'b0);
  and and_93 (and_93_out, and_19_out, 1'b0);
  and and_94 (and_94_out, and_19_out, 1'b0);
  and and_95 (and_95_out, and_22_out, 1'b0);
  and and_96 (and_96_out, and_22_out, 1'b1);
  and and_97 (and_97_out, and_25_out, 1'b0);
  and and_98 (and_98_out, and_25_out, 1'b0);
  and and_99 (and_99_out, and_28_out, 1'b1);
  and and_100 (and_100_out, and_28_out, 1'b0);
  and and_101 (and_101_out, and_31_out, 1'b0);
  and and_102 (and_102_out, and_31_out, 1'b0);
  and and_103 (and_103_out, and_34_out, 1'b0);
  and and_104 (and_104_out, and_34_out, 1'b1);
  and and_105 (and_105_out, and_37_out, 1'b0);
  and and_106 (and_106_out, and_37_out, 1'b0);
  and and_107 (and_107_out, and_40_out, 1'b1);
  and and_108 (and_108_out, and_40_out, 1'b0);
  and and_109 (and_109_out, and_43_out, 1'b0);
  and and_110 (and_110_out, and_43_out, 1'b1);
  and and_111 (and_111_out, and_46_out, 1'b1);
  and and_112 (and_112_out, and_46_out, 1'b1);
  and and_113 (and_113_out, and_1_out, 1'b1);
  and and_114 (and_114_out, and_1_out, 1'b1);
  and and_115 (and_115_out, and_4_out, 1'b1);
  and and_116 (and_116_out, and_4_out, 1'b0);
  and and_117 (and_117_out, and_7_out, 1'b0);
  and and_118 (and_118_out, and_7_out, 1'b1);
  and and_119 (and_119_out, and_10_out, 1'b1);
  and and_120 (and_120_out, and_10_out, 1'b0);
  and and_121 (and_121_out, and_13_out, 1'b1);
  and and_122 (and_122_out, and_13_out, 1'b1);
  and and_123 (and_123_out, and_16_out, 1'b1);
  and and_124 (and_124_out, and_16_out, 1'b0);
  and and_125 (and_125_out, and_19_out, 1'b1);
  and and_126 (and_126_out, and_19_out, 1'b0);
  and and_127 (and_127_out, and_22_out, 1'b1);
  and and_128 (and_128_out, and_22_out, 1'b0);
  and and_129 (and_129_out, and_25_out, 1'b0);
  and and_130 (and_130_out, and_25_out, 1'b1);
  and and_131 (and_131_out, and_28_out, 1'b0);
  and and_132 (and_132_out, and_28_out, 1'b0);
  and and_133 (and_133_out, and_31_out, 1'b0);
  and and_134 (and_134_out, and_31_out, 1'b0);
  and and_135 (and_135_out, and_34_out, 1'b0);
  and and_136 (and_136_out, and_34_out, 1'b0);
  and and_137 (and_137_out, and_37_out, 1'b0);
  and and_138 (and_138_out, and_37_out, 1'b1);
  and and_139 (and_139_out, and_40_out, 1'b1);
  and and_140 (and_140_out, and_40_out, 1'b0);
  and and_141 (and_141_out, and_43_out, 1'b0);
  and and_142 (and_142_out, and_43_out, 1'b0);
  and and_143 (and_143_out, and_46_out, 1'b1);
  and and_144 (and_144_out, and_46_out, 1'b1);
  ROMyou romyou_1 (
    .in_9(and_113_out), .in_10(and_114_out), .in_11(and_81_out), .in_12(and_82_out), .in_13(and_50_out),
    .in_14(and_49_out), .in_15(and_3_out), .in_16(and_2_out), .in_1(1'b0), .in_2(1'b0), .in_3(1'b0),
    .in_4(1'b0), .in_5(1'b0), .in_6(1'b0), .in_7(1'b0), .in_8(1'b0), .out_17(romyou_1_out_17),
    .out_18(romyou_1_out_18), .out_19(romyou_1_out_19), .out_20(romyou_1_out_20), .out_21(romyou_1_out_21),
    .out_22(romyou_1_out_22), .out_23(romyou_1_out_23), .out_24(romyou_1_out_24));
  ROMyou romyou_2 (
    .in_9(and_115_out), .in_10(and_116_out), .in_11(and_83_out), .in_12(and_84_out), .in_13(and_52_out),
    .in_14(and_51_out), .in_15(and_5_out), .in_16(and_6_out), .in_1(romyou_1_out_17), .in_2(romyou_1_out_18),
    .in_3(romyou_1_out_19), .in_4(romyou_1_out_20), .in_5(romyou_1_out_21), .in_6(romyou_1_out_22),
    .in_7(romyou_1_out_23), .in_8(romyou_1_out_24), .out_17(romyou_2_out_17), .out_18(romyou_2_out_18),
    .out_19(romyou_2_out_19), .out_20(romyou_2_out_20), .out_21(romyou_2_out_21), .out_22(romyou_2_out_22),
    .out_23(romyou_2_out_23), .out_24(romyou_2_out_24));
  ROMyou romyou_3 (
    .in_9(and_118_out), .in_10(and_117_out), .in_11(and_85_out), .in_12(and_86_out), .in_13(and_53_out),
    .in_14(and_54_out), .in_15(and_8_out), .in_16(and_9_out), .in_1(romyou_2_out_17), .in_2(romyou_2_out_18),
    .in_3(romyou_2_out_19), .in_4(romyou_2_out_20), .in_5(romyou_2_out_21), .in_6(romyou_2_out_22),
    .in_7(romyou_2_out_23), .in_8(romyou_2_out_24), .out_17(romyou_3_out_17), .out_18(romyou_3_out_18),
    .out_19(romyou_3_out_19), .out_20(romyou_3_out_20), .out_21(romyou_3_out_21), .out_22(romyou_3_out_22),
    .out_23(romyou_3_out_23), .out_24(romyou_3_out_24));
  ROMyou romyou_4 (
    .in_9(and_119_out), .in_10(and_120_out), .in_11(and_88_out), .in_12(and_87_out), .in_13(and_55_out),
    .in_14(and_56_out), .in_15(and_12_out), .in_16(and_11_out), .in_1(romyou_3_out_17),
    .in_2(romyou_3_out_18), .in_3(romyou_3_out_19), .in_4(romyou_3_out_20), .in_5(romyou_3_out_21),
    .in_6(romyou_3_out_22), .in_7(romyou_3_out_23), .in_8(romyou_3_out_24), .out_17(romyou_4_out_17),
    .out_18(romyou_4_out_18), .out_19(romyou_4_out_19), .out_20(romyou_4_out_20), .out_21(romyou_4_out_21),
    .out_22(romyou_4_out_22), .out_23(romyou_4_out_23), .out_24(romyou_4_out_24));
  ROMyou romyou_5 (
    .in_9(and_121_out), .in_10(and_122_out), .in_11(and_90_out), .in_12(and_89_out), .in_13(and_58_out),
    .in_14(and_57_out), .in_15(and_14_out), .in_16(and_15_out), .in_1(romyou_4_out_17),
    .in_2(romyou_4_out_18), .in_3(romyou_4_out_19), .in_4(romyou_4_out_20), .in_5(romyou_4_out_21),
    .in_6(romyou_4_out_22), .in_7(romyou_4_out_23), .in_8(romyou_4_out_24), .out_17(romyou_5_out_17),
    .out_18(romyou_5_out_18), .out_19(romyou_5_out_19), .out_20(romyou_5_out_20), .out_21(romyou_5_out_21),
    .out_22(romyou_5_out_22), .out_23(romyou_5_out_23), .out_24(romyou_5_out_24));
  ROMyou romyou_6 (
    .in_9(and_124_out), .in_10(and_123_out), .in_11(and_91_out), .in_12(and_92_out), .in_13(and_60_out),
    .in_14(and_59_out), .in_15(and_18_out), .in_16(and_17_out), .in_1(romyou_5_out_17),
    .in_2(romyou_5_out_18), .in_3(romyou_5_out_19), .in_4(romyou_5_out_20), .in_5(romyou_5_out_21),
    .in_6(romyou_5_out_22), .in_7(romyou_5_out_23), .in_8(romyou_5_out_24), .out_17(romyou_6_out_17),
    .out_18(romyou_6_out_18), .out_19(romyou_6_out_19), .out_20(romyou_6_out_20), .out_21(romyou_6_out_21),
    .out_22(romyou_6_out_22), .out_23(romyou_6_out_23), .out_24(romyou_6_out_24));
  ROMyou romyou_7 (
    .in_9(and_125_out), .in_10(and_126_out), .in_11(and_94_out), .in_12(and_93_out), .in_13(and_62_out),
    .in_14(and_61_out), .in_15(and_21_out), .in_16(and_20_out), .in_1(romyou_6_out_17),
    .in_2(romyou_6_out_18), .in_3(romyou_6_out_19), .in_4(romyou_6_out_20), .in_5(romyou_6_out_21),
    .in_6(romyou_6_out_22), .in_7(romyou_6_out_23), .in_8(romyou_6_out_24), .out_17(romyou_7_out_17),
    .out_18(romyou_7_out_18), .out_19(romyou_7_out_19), .out_20(romyou_7_out_20), .out_21(romyou_7_out_21),
    .out_22(romyou_7_out_22), .out_23(romyou_7_out_23), .out_24(romyou_7_out_24));
  ROMyou romyou_8 (
    .in_9(and_128_out), .in_10(and_127_out), .in_11(and_96_out), .in_12(and_95_out), .in_13(and_63_out),
    .in_14(and_64_out), .in_15(and_23_out), .in_16(and_24_out), .in_1(romyou_7_out_17),
    .in_2(romyou_7_out_18), .in_3(romyou_7_out_19), .in_4(romyou_7_out_20), .in_5(romyou_7_out_21),
    .in_6(romyou_7_out_22), .in_7(romyou_7_out_23), .in_8(romyou_7_out_24), .out_17(romyou_8_out_17),
    .out_18(romyou_8_out_18), .out_19(romyou_8_out_19), .out_20(romyou_8_out_20), .out_21(romyou_8_out_21),
    .out_22(romyou_8_out_22), .out_23(romyou_8_out_23), .out_24(romyou_8_out_24));
  ROMyou romyou_9 (
    .in_9(and_130_out), .in_10(and_129_out), .in_11(and_97_out), .in_12(and_98_out), .in_13(and_65_out),
    .in_14(and_66_out), .in_15(and_27_out), .in_16(and_26_out), .in_1(romyou_8_out_17),
    .in_2(romyou_8_out_18), .in_3(romyou_8_out_19), .in_4(romyou_8_out_20), .in_5(romyou_8_out_21),
    .in_6(romyou_8_out_22), .in_7(romyou_8_out_23), .in_8(romyou_8_out_24), .out_17(romyou_9_out_17),
    .out_18(romyou_9_out_18), .out_19(romyou_9_out_19), .out_20(romyou_9_out_20), .out_21(romyou_9_out_21),
    .out_22(romyou_9_out_22), .out_23(romyou_9_out_23), .out_24(romyou_9_out_24));
  ROMyou romyou_10 (
    .in_9(and_132_out), .in_10(and_131_out), .in_11(and_100_out), .in_12(and_99_out), .in_13(and_67_out),
    .in_14(and_68_out), .in_15(and_30_out), .in_16(and_29_out), .in_1(romyou_9_out_17),
    .in_2(romyou_9_out_18), .in_3(romyou_9_out_19), .in_4(romyou_9_out_20), .in_5(romyou_9_out_21),
    .in_6(romyou_9_out_22), .in_7(romyou_9_out_23), .in_8(romyou_9_out_24), .out_17(romyou_10_out_17),
    .out_18(romyou_10_out_18), .out_19(romyou_10_out_19), .out_20(romyou_10_out_20),
    .out_21(romyou_10_out_21), .out_22(romyou_10_out_22), .out_23(romyou_10_out_23), .out_24(romyou_10_out_24));
  ROMyou romyou_11 (
    .in_9(and_134_out), .in_10(and_133_out), .in_11(and_101_out), .in_12(and_102_out), .in_13(and_69_out),
    .in_14(and_70_out), .in_15(and_32_out), .in_16(and_33_out), .in_1(romyou_10_out_17),
    .in_2(romyou_10_out_18), .in_3(romyou_10_out_19), .in_4(romyou_10_out_20), .in_5(romyou_10_out_21),
    .in_6(romyou_10_out_22), .in_7(romyou_10_out_23), .in_8(romyou_10_out_24), .out_17(romyou_11_out_17),
    .out_18(romyou_11_out_18), .out_19(romyou_11_out_19), .out_20(romyou_11_out_20),
    .out_21(romyou_11_out_21), .out_22(romyou_11_out_22), .out_23(romyou_11_out_23), .out_24(romyou_11_out_24));
  ROMyou romyou_12 (
    .in_9(and_135_out), .in_10(and_136_out), .in_11(and_104_out), .in_12(and_103_out), .in_13(and_72_out),
    .in_14(and_71_out), .in_15(and_36_out), .in_16(and_35_out), .in_1(romyou_11_out_17),
    .in_2(romyou_11_out_18), .in_3(romyou_11_out_19), .in_4(romyou_11_out_20), .in_5(romyou_11_out_21),
    .in_6(romyou_11_out_22), .in_7(romyou_11_out_23), .in_8(romyou_11_out_24), .out_17(romyou_12_out_17),
    .out_18(romyou_12_out_18), .out_19(romyou_12_out_19), .out_20(romyou_12_out_20),
    .out_21(romyou_12_out_21), .out_22(romyou_12_out_22), .out_23(romyou_12_out_23), .out_24(romyou_12_out_24));
  ROMyou romyou_13 (
    .in_9(and_138_out), .in_10(and_137_out), .in_11(and_105_out), .in_12(and_106_out), .in_13(and_73_out),
    .in_14(and_74_out), .in_15(and_38_out), .in_16(and_39_out), .in_1(romyou_12_out_17),
    .in_2(romyou_12_out_18), .in_3(romyou_12_out_19), .in_4(romyou_12_out_20), .in_5(romyou_12_out_21),
    .in_6(romyou_12_out_22), .in_7(romyou_12_out_23), .in_8(romyou_12_out_24), .out_17(romyou_13_out_17),
    .out_18(romyou_13_out_18), .out_19(romyou_13_out_19), .out_20(romyou_13_out_20),
    .out_21(romyou_13_out_21), .out_22(romyou_13_out_22), .out_23(romyou_13_out_23), .out_24(romyou_13_out_24));
  ROMyou romyou_14 (
    .in_9(and_140_out), .in_10(and_139_out), .in_11(and_108_out), .in_12(and_107_out), .in_13(and_76_out),
    .in_14(and_75_out), .in_15(and_41_out), .in_16(and_42_out), .in_1(romyou_13_out_17),
    .in_2(romyou_13_out_18), .in_3(romyou_13_out_19), .in_4(romyou_13_out_20), .in_5(romyou_13_out_21),
    .in_6(romyou_13_out_22), .in_7(romyou_13_out_23), .in_8(romyou_13_out_24), .out_17(romyou_14_out_17),
    .out_18(romyou_14_out_18), .out_19(romyou_14_out_19), .out_20(romyou_14_out_20),
    .out_21(romyou_14_out_21), .out_22(romyou_14_out_22), .out_23(romyou_14_out_23), .out_24(romyou_14_out_24));
  ROMyou romyou_15 (
    .in_9(and_142_out), .in_10(and_141_out), .in_11(and_109_out), .in_12(and_110_out), .in_13(and_78_out),
    .in_14(and_77_out), .in_15(and_45_out), .in_16(and_44_out), .in_1(romyou_14_out_17),
    .in_2(romyou_14_out_18), .in_3(romyou_14_out_19), .in_4(romyou_14_out_20), .in_5(romyou_14_out_21),
    .in_6(romyou_14_out_22), .in_7(romyou_14_out_23), .in_8(romyou_14_out_24), .out_17(romyou_15_out_17),
    .out_18(romyou_15_out_18), .out_19(romyou_15_out_19), .out_20(romyou_15_out_20),
    .out_21(romyou_15_out_21), .out_22(romyou_15_out_22), .out_23(romyou_15_out_23), .out_24(romyou_15_out_24));
  ROMyou romyou_16 (
    .in_9(and_143_out), .in_10(and_144_out), .in_11(and_111_out), .in_12(and_112_out), .in_13(and_79_out),
    .in_14(and_80_out), .in_15(and_48_out), .in_16(and_47_out), .in_1(romyou_15_out_17),
    .in_2(romyou_15_out_18), .in_3(romyou_15_out_19), .in_4(romyou_15_out_20), .in_5(romyou_15_out_21),
    .in_6(romyou_15_out_22), .in_7(romyou_15_out_23), .in_8(romyou_15_out_24), .out_17(out_2[3]),
    .out_18(out_2[2]), .out_19(out_2[1]), .out_20(out_2[0]), .out_21(out_3[3]), .out_22(out_3[2]),
    .out_23(out_3[1]), .out_24(out_3[0]));
endmodule

// RGST
module Register (
  input  RST_minus,
  input  CLK,
  input  [3:0] SELECT_L,
  input  [3:0] ABCD_in,
  input  [1:0] SELECT_AB,
  input  [3:0] in_6,
  input  SW_0,
  input  SW_1,
  input  SW_2,
  input  SW_3,
  output LED_0,
  output LED_1,
  output LED_2,
  output LED_3,
  output PRG_0,
  output PRG_1,
  output PRG_2,
  output PRG_3
);

  wire A_p8, A_p9, A_p10, A_p11, A_p12, B_p8, B_p9, B_p10, B_p11, B_p12, C_p8, D_p8, n74153_1_p7,
       n74153_1_p14, n74153_2_p7, n74153_2_p14, not_1_out;

  not not_1 (not_1_out, RST_minus);
  // _74161 A: pin names not known; wires that end beside it: not_1_out, CLK, ABCD_in[0], ABCD_in[1], ABCD_in[2], ABCD_in[3], 1'b0, A_p8, A_p9, A_p10, A_p11, A_p12, 1'b0, SELECT_L[3], A_p8
  // _74161 B: pin names not known; wires that end beside it: not_1_out, CLK, ABCD_in[0], ABCD_in[1], ABCD_in[2], ABCD_in[3], 1'b0, B_p8, B_p9, B_p10, B_p11, B_p12, 1'b0, SELECT_L[2], B_p8
  // _74161 C: pin names not known; wires that end beside it: not_1_out, CLK, ABCD_in[0], ABCD_in[1], ABCD_in[2], ABCD_in[3], 1'b0, C_p8, LED_0, LED_1, LED_2, LED_3, 1'b0, SELECT_L[1], C_p8
  // _74153 74153_1: pin names not known; wires that end beside it: 1'b0, SELECT_AB[1], 1'b0, SW_0, B_p9, A_p9, n74153_1_p7, 1'b0, SELECT_AB[0], 1'b0, SW_1, B_p10, A_p10, n74153_1_p14
  // _74161 D: pin names not known; wires that end beside it: not_1_out, CLK, ABCD_in[0], ABCD_in[1], ABCD_in[2], ABCD_in[3], 1'b1, D_p8, PRG_0, PRG_1, PRG_2, PRG_3, 1'b1, SELECT_L[0], D_p8
  // _74153 74153_2: pin names not known; wires that end beside it: 1'b0, SELECT_AB[1], 1'b0, SW_2, B_p11, A_p11, n74153_2_p7, 1'b0, SELECT_AB[0], 1'b0, SW_3, B_p12, A_p12, n74153_2_p14, n74153_2_p7, n74153_2_p14, n74153_1_p7, n74153_1_p14
endmodule

module Register_2 (
  input  RST_minus,
  input  CLK,
  input  [3:0] Select_Register,
  input  [3:0] Register_num_in,
  input  [1:0] SELECT_AB,
  input  [3:0] Import,
  output [3:0] Outport,
  output [3:0] Address_num,
  output [3:0] Register_num_out
);

  wire A_p8, A_p9, A_p10, A_p11, A_p12, B_p8, B_p9, B_p10, B_p11, B_p12, C_p8, D_p8, not_1_out;

  not not_1 (not_1_out, RST_minus);
  // _74161 A: pin names not known; wires that end beside it: not_1_out, CLK, Register_num_in[0], Register_num_in[1], Register_num_in[2], Register_num_in[3], 1'b0, A_p8, A_p9, A_p10, A_p11, A_p12, 1'b0, Select_Register[3], A_p8
  // _74161 B: pin names not known; wires that end beside it: not_1_out, CLK, Register_num_in[0], Register_num_in[1], Register_num_in[2], Register_num_in[3], 1'b0, B_p8, B_p9, B_p10, B_p11, B_p12, 1'b0, Select_Register[2], B_p8
  // _74161 C: pin names not known; wires that end beside it: not_1_out, CLK, Register_num_in[0], Register_num_in[1], Register_num_in[2], Register_num_in[3], 1'b0, C_p8, Outport[0], Outport[1], Outport[2], Outport[3], 1'b0, Select_Register[1], C_p8
  // _74153 74153_1: pin names not known; wires that end beside it: 1'b0, SELECT_AB[1], 1'b0, Import[0], B_p9, A_p9, Register_num_out[2], 1'b0, SELECT_AB[0], 1'b0, Import[1], B_p10, A_p10, Register_num_out[3]
  // _74161 D: pin names not known; wires that end beside it: not_1_out, CLK, Register_num_in[0], Register_num_in[1], Register_num_in[2], Register_num_in[3], 1'b1, D_p8, Address_num[0], Address_num[1], Address_num[2], Address_num[3], 1'b1, Select_Register[0], D_p8
  // _74153 74153_2: pin names not known; wires that end beside it: 1'b0, SELECT_AB[1], 1'b0, Import[2], B_p11, A_p11, Register_num_out[0], 1'b0, SELECT_AB[0], 1'b0, Import[3], B_p12, A_p12, Register_num_out[1]
endmodule

module TD4 (
  input  in_1,
  input  in_2,
  input  in_3,
  input  in_4
);

  wire clock_1_out, decorder_1_p1, decorder_1_p2, decorder_1_p3, decorder_1_p4, n74283_1_c4, register_1_p3,
       register_1_p4, register_1_p5, register_1_p6, register_1_p7, register_1_p8, register_1_p13,
       register_1_p14, register_1_p15, register_1_p16, register_1_p17, register_1_p18, register_1_p19,
       register_1_p20, register_1_p21, register_1_p22, register_1_p23, register_1_p24, register_1_p25,
       register_1_p26, register_1_p27, register_1_p28, Reset_out, rom_1_p1, rom_1_p8, undriven, undriven_2,
       undriven_3;

  Button Reset (.out(Reset_out));
  Clock clock_1 (.out(clock_1_out));
  // Decorder decorder_1: pin names not known; wires that end beside it: decorder_1_p1, decorder_1_p2, decorder_1_p3, decorder_1_p4
  D_Flip_Flop #(.trigger("high")) d_ff_1 (
    .clk(clock_1_out), .D(n74283_1_c4), .Q(decorder_1_p4));  // open: Qn, preset, en, reset
  // Register register_1: pin names not known; wires that end beside it: Reset_out, clock_1_out, register_1_p3, register_1_p4, register_1_p5, register_1_p6, register_1_p7, register_1_p8, in_1, in_2, in_3, in_4, register_1_p13, register_1_p14, register_1_p15, register_1_p16, register_1_p17, register_1_p18, register_1_p19, register_1_p20, register_1_p21, register_1_p22, register_1_p23, register_1_p24, register_1_p25, register_1_p26, register_1_p27, register_1_p28
  // ROM rom_1: pin names not known; wires that end beside it: rom_1_p1, decorder_1_p1, register_1_p13, decorder_1_p2, register_1_p14, decorder_1_p3, register_1_p15, rom_1_p8
  _74283 u_74283_1 (
    .C0(1'b0), .A1(register_1_p25), .A2(register_1_p26), .A3(register_1_p27), .A4(register_1_p28),
    .B1(undriven_2), .B2(undriven_3), .B3(undriven), .B4(rom_1_p8), .\Σ1 (register_1_p24),
    .\Σ2 (register_1_p23), .\Σ3 (register_1_p22), .\Σ4 (register_1_p21), .C4(n74283_1_c4));
  LED led_1 (.in(register_1_p17));
  LED led_2 (.in(register_1_p18));
  LED led_3 (.in(register_1_p20));
  LED led_4 (.in(register_1_p19));
endmodule

module TD4_2 (
  input  [3:0] in_1
);

  wire button_1_out, clock_1_out, d_ff_1_q, n4bit_adder_2_1_c4;
  wire [1:0] decorder_2_1_select_ab;
  wire [3:0] decorder_2_1_select_register, n4bit_adder_2_1_out_4, register_2_1_address_num,
       register_2_1_outport, register_2_1_register_num_out, rom_2_1_out_2, rom_2_1_out_3;

  DotMatrix #(.matrixcols(4), .matrixrows(1)) dotmatrix_1 (
    .col0(decorder_2_1_select_register[3]), .col1(decorder_2_1_select_register[2]),
    .col2(decorder_2_1_select_register[1]), .col3(decorder_2_1_select_register[0]));
  DotMatrix #(.matrixcols(4), .matrixrows(1)) dotmatrix_2 (
    .col0(rom_2_1_out_2[3]), .col1(rom_2_1_out_2[2]), .col2(rom_2_1_out_2[1]), .col3(rom_2_1_out_2[0]));
  Button button_1 (.out(button_1_out));
  Clock clock_1 (.out(clock_1_out));
  Decorder_2 decorder_2_1 (
    .OPCord(rom_2_1_out_2), .C_Flag_minus(d_ff_1_q), .SELECT_Register(decorder_2_1_select_register),
    .SELECT_AB(decorder_2_1_select_ab));
  ROM_2 rom_2_1 (.Address_in(register_2_1_address_num), .out_2(rom_2_1_out_2), .out_3(rom_2_1_out_3));
  DotMatrix #(.matrixcols(4), .matrixrows(1)) dotmatrix_3 (
    .col0(register_2_1_address_num[3]), .col1(register_2_1_address_num[2]),
    .col2(register_2_1_address_num[1]), .col3(register_2_1_address_num[0]));
  D_Flip_Flop d_ff_1 (
    .clk(clock_1_out), .D(n4bit_adder_2_1_c4), .Q(d_ff_1_q), .preset(button_1_out));  // open: Qn, en, reset
  Register_2 register_2_1 (
    .RST_minus(button_1_out), .CLK(clock_1_out), .Select_Register(decorder_2_1_select_register),
    .Register_num_in(n4bit_adder_2_1_out_4), .SELECT_AB(decorder_2_1_select_ab), .Import(in_1),
    .Outport(register_2_1_outport), .Address_num(register_2_1_address_num),
    .Register_num_out(register_2_1_register_num_out));
  _4bit_Adder_2 u_4bit_adder_2_1 (
    .C0(1'b0), .A_num(register_2_1_register_num_out), .B_num(rom_2_1_out_3), .out_4(n4bit_adder_2_1_out_4),
    .C4(n4bit_adder_2_1_c4));
  DotMatrix #(.matrixcols(4), .matrixrows(1)) dotmatrix_4 (
    .col0(rom_2_1_out_3[3]), .col1(rom_2_1_out_3[2]), .col2(rom_2_1_out_3[1]), .col3(rom_2_1_out_3[0]));
  DotMatrix #(.matrixcols(4), .matrixrows(1)) dotmatrix_5 (
    .col0(register_2_1_outport[3]), .col1(register_2_1_outport[2]), .col2(register_2_1_outport[1]),
    .col3(register_2_1_outport[0]));
endmodule
